# Fritzing sketch E6B2-CWZ6C (saved by Fritzing 0.9.3b)
circuit board: 8.46667cm x 5.64444cm
breadboards: 1

parts:
  Raspberry_Pi_1 = Raspberry Pi 3 [part_number=RPI-3-V1.2]
  RE1 = Rotary Encoder [package=THT]
  R1 = Resistor [tolerance=±5% resistance=220 package="0603 [SMD]"]
  R2 = Resistor [tolerance=±5% resistance=220 package="0603 [SMD]"]

nets:
  N1: Raspberry_Pi_1.GIPO17, RE1.EncoderPinA, R1.Pin_1
  N2: Raspberry_Pi_1.GIPO27, RE1.EncoderPinB, R2.Pin_1
  N3: Raspberry_Pi_1.5V, R1.Pin_0, R2.Pin_0

notes:
  Blue: GND
  Shield: GND
  Black: A
  White: B
  5V
  Brown: 5V
  Blue: GND
  Shield: GND
  Black: A
  White: B
