# Fritzing sketch MOS Driver (saved by Fritzing 0.9.3b)
breadboards: 1

parts:
  V1 = DC Power [voltage=12V]
  Q1_MDP12N50F = MOSFET-NCHANNEL [package=sot23-3]
  M1 = DC Motor
  C1 = Capacitor [package=0603-cap]
  R1 = Resistor [tolerance=±5% resistance=330 package=THT]
  Q1_MMBT3906 = NPN-Transistor [package="TO92 [THT]"]
  Q2_MMBT3906 = PNP-Transistor [package="SOT-23 [SMD]"]
  R2 = Resistor [tolerance=±5% resistance=6.8k package=THT]
  R3 = Resistor [tolerance=±5% resistance=6.8k package=THT]
  C1_2 = Capacitor [package=0805]
  C1_Cgs = Capacitor [package=1206]

nets:
  N1: V1.V+, M1.pin_1, Q1_MMBT3906.C
  N2: Q1_MDP12N50F.G, C1.1, R1.Pin_1, C1_2.1, C1_Cgs.1
  GND: Q1_MDP12N50F.S, C1.2, Q2_MMBT3906.1, C1_2.2, C1_Cgs.2
  N3: Q1_MDP12N50F.D, M1.pin_2
  N4: R1.Pin_0, Q1_MMBT3906.E, Q2_MMBT3906.2
  N5: Q1_MMBT3906.B, R2.Pin_1
  N6: Q2_MMBT3906.0, R3.Pin_1
  N7: R2.Pin_0, R3.Pin_0
