# Fritzing sketch PCR (saved by Fritzing 0.9.2b)
breadboards: 1

parts:
  U1 = TLP621 [part_number=TLP421A package=THT]
  RL = Resistor [tolerance=±5% resistance=330 package=THT]
  U2 = TLP621 [part_number=TLP421A package=THT]
  RL1 = Resistor [tolerance=±5% resistance=330 package=THT]
  U3 = TLP621 [part_number=TLP421A package=THT]
  RL2 = Resistor [tolerance=±5% resistance=330 package=THT]
  R1 = Resistor [tolerance=±5% resistance=100 package=THT]
  R2 = Rotary Potentiometer (Small) [maximum_resistance=1kΩ package=THT]
  D1 = Rectifier Diode [package="300 mil [THT]"]
  R7 = Resistor [tolerance=±5% resistance=1k package=THT]
  IC2 = IC, DIP package, 16 pins [chip_label=MCP3008 part_number=ADC]
  R3 = Resistor [tolerance=±5% resistance=100 package=THT]
  R4 = Rotary Potentiometer (Small) [maximum_resistance=1kΩ package=THT]
  D2 = Rectifier Diode [package="300 mil [THT]"]
  R8 = Resistor [tolerance=±5% resistance=1k package=THT]
  R5 = Resistor [tolerance=±5% resistance=100 package=THT]
  R6 = Rotary Potentiometer (Small) [maximum_resistance=1kΩ package=THT]
  D3 = Rectifier Diode [package="300 mil [THT]"]
  R9 = Resistor [tolerance=±5% resistance=1k package=THT]
  IC1 = IC, DIP package, 8 pins [chip_label=LM334]
  IC3 = IC, DIP package, 8 pins [chip_label=LM334]
  IC4 = IC, DIP package, 8 pins [chip_label=LM334]

nets:
  RPi GPIO: U1.Pin_1, U2.Pin_1, U3.Pin_1
  GND: U1.Pin_2, U1.Pin_3, U2.Pin_2, U2.Pin_3, U3.Pin_2, U3.Pin_3, R7.Pin_1, IC2.pin3, IC2.pin5, IC2.pin7, IC2.pin16, R8.Pin_1, R9.Pin_1
  N1: U1.Pin_4, RL.Pin_0
  12V: RL.Pin_1, RL1.Pin_1, RL2.Pin_1
  N2: U2.Pin_4, RL1.Pin_0
  N3: U3.Pin_4, RL2.Pin_0
  N4: R1.Pin_0, R2.leg2, D1.anode, IC1.pin2
  N5: R1.Pin_1, IC1.pin1
  N6: R2.wiper, D1.cathode, R7.Pin_0, IC2.pin8
  N7: IC2.pin4, R6.wiper, D3.cathode, R9.Pin_0
  N8: IC2.pin6, R4.wiper, D2.cathode, R8.Pin_0
  SPI: IC2.pin9, IC2.pin10, IC2.pin11, IC2.pin12, IC2.pin13
  5V: IC2.pin14, IC1.pin3, IC3.pin3, IC4.pin3
  3.3V: IC2.pin15
  N9: R3.Pin_0, R4.leg2, D2.anode, IC3.pin2
  N10: R3.Pin_1, IC3.pin1
  N11: R5.Pin_0, R6.leg2, D3.anode, IC4.pin2
  N12: R5.Pin_1, IC4.pin1

notes:
  SPI to Rspebrry Pi
  PCR 回路図　キ ヨク, フォットカプラU1,U2,U3実際の型番はTLP421A, V2
  1mA
  →
