# Fritzing sketch Switch_Input_Sequences (saved by Fritzing 0.9.3b)
breadboards: 1

parts:
  Raspberry_Pi1 = Raspberry Pi B+
  S1 = Pushbutton [package="[THT]"]
  S2 = Pushbutton [package="[THT]"]
  S3 = Pushbutton [package="[THT]"]
  S4 = Pushbutton [package="[THT]"]
  R1 = Resistor [tolerance=±5% resistance=220 package="0402 [SMD]"]
  R2 = Resistor [tolerance=±5% resistance=220 package="0402 [SMD]"]
  R3 = Resistor [tolerance=±5% resistance=220 package="0402 [SMD]"]
  R4 = Resistor [tolerance=±5% resistance=220 package="0402 [SMD]"]
  R5 = Resistor [tolerance=±5% resistance=220 package="0402 [SMD]"]
  R6 = Resistor [tolerance=±5% resistance=220 package="0402 [SMD]"]
  R7 = Resistor [tolerance=±5% resistance=220 package="0402 [SMD]"]
  R8 = Resistor [tolerance=±5% resistance=220 package="0402 [SMD]"]
  LED1 = smd LED [color="Red (633nm)" package="1206 [SMD]"]
  LED2 = LED - 3mm [color="Red (633nm)" package="3 mm [THT]"]
  LED3 = LED - 3mm [color="Red (633nm)" package="3 mm [THT]"]
  LED4 = LED - 3mm [color="Red (633nm)" package="3 mm [THT]"]

nets:
  N1: Raspberry_Pi1.GPIO10, LED4.anode
  N2: Raspberry_Pi1.GPIO9, LED3.anode
  N3: Raspberry_Pi1.GPIO11, LED2.anode
  N4: Raspberry_Pi1.GPIO13, LED1.anode
  N5: Raspberry_Pi1.GPIO20, Raspberry_Pi1.GPIO16, S1.Pin_1, S1.Pin_2, R2.Pin_1
  N6: Raspberry_Pi1.GPIO7, S2.Pin_1, S2.Pin_2, R4.Pin_1
  N7: Raspberry_Pi1.GPIO8, S3.Pin_1, S3.Pin_2, R6.Pin_1
  N8: Raspberry_Pi1.GPIO23, S4.Pin_1, S4.Pin_2, R8.Pin_1
  N9: Raspberry_Pi1.GPIO14, Raspberry_Pi1.GND, R2.Pin_0, R4.Pin_0, R6.Pin_0, R8.Pin_0, LED1.cathode, LED2.cathode, LED3.cathode, LED4.cathode
  N10: Raspberry_Pi1.5V, R1.Pin_0, R3.Pin_0, R5.Pin_0, R7.Pin_0
  N11: S1.Pin_3, S1.Pin_4, R1.Pin_1
  N12: S2.Pin_3, S2.Pin_4, R3.Pin_1
  N13: S3.Pin_3, S3.Pin_4, R5.Pin_1
  N14: S4.Pin_3, S4.Pin_4, R7.Pin_1
