# Fritzing sketch 马达-按键控制 (saved by Fritzing 0.9.3b)
breadboards: 1

parts:
  Raspberry_Pi_1 = Raspberry Pi 3 [part_number=RPI-3-V1.2]
  S1 = Pushbutton [package="[SMD]"]
  S2 = Pushbutton [package="[SMD]"]
  S3 = Pushbutton [package="[SMD]"]
  R1 = Resistor [tolerance=±5% resistance=220 package="1206 [SMD]"]
  R2 = Resistor [tolerance=±5% resistance=220 package="1206 [SMD]"]
  R3 = Resistor [tolerance=±5% resistance=220 package="1206 [SMD]"]
  R4 = Resistor [tolerance=±5% resistance=220 package="1206 [SMD]"]
  R5 = Resistor [tolerance=±5% resistance=220 package="1206 [SMD]"]
  R6 = Resistor [tolerance=±5% resistance=220 package="1206 [SMD]"]

nets:
  N1: Raspberry_Pi_1.GIPO16, S1.Pin_1, S1.Pin_2, R2.Pin_1
  N2: Raspberry_Pi_1.GIPO7, S2.Pin_1, S2.Pin_2, R4.Pin_1
  N3: Raspberry_Pi_1.GIPO18, S3.Pin_1, S3.Pin_2, R6.Pin_1
  N4: S1.Pin_3, S1.Pin_4, R1.Pin_1
  N5: S2.Pin_3, S2.Pin_4, R3.Pin_1
  N6: S3.Pin_3, S3.Pin_4, R5.Pin_1
  N7: R1.Pin_0, R3.Pin_0, R5.Pin_0
  N8: R2.Pin_0, R4.Pin_0, R6.Pin_0

notes:
  正転
  逆転
  停止
  +5V
  GND
